# Fritzing sketch Solar (saved by Fritzing 0.9.2b)
perfboards: 1

parts:
  U1 = atmega328 [package=dip]
  C1 = Electrolytic Capacitor [capacitance=1mF package="300 mil [THT, electrolytic]"]
  D1 = DIODE-SCHOTTKY [package=sma-diode]
  R1 = Resistor [tolerance=±5% resistance=330 package=THT]
  LED1 = LED - 5mm [color="Red (633nm)" package="5 mm [THT]"]
  R2 = Resistor [tolerance=±5% resistance=220k package=THT]
  R3 = Photocell (LDR) [package=THT]
  U2 = Voltage Regulator [package=to220-adj]
  C2 = Ceramic Capacitor [capacitance=1µF package="100 mil [THT, multilayer]"]
  C3 = Ceramic Capacitor [capacitance=1µF package="100 mil [THT, multilayer]"]
  D2 = Diode [package=diode-1n4001]  # not connected

nets (from the schematic view):
  N1: U1.VCC, U1.AVCC, C1.+, D1.C, U2.IN, C2.1
  GND: U1.GND, C1.-, D1.A, LED1.cathode, R2.Pin_1, U2.ADJ, C2.0, C3.0
  N2: U1.D7, R3.pin_1
  N3: U1.D8, R1.Pin_1
  N4: U1.A0, R2.Pin_0, R3.pin_0
  N5: R1.Pin_0, LED1.anode
  N6: U2.OUT, C3.1
